# Fritzing sketch DHT22 -ESP8266 (saved by Fritzing 0.9.3b)
breadboards: 1

parts:
  ESP = ESP8266-12 [part_number=ESP8266-12]
  R1 = Resistor [tolerance=±5% resistance=10k package=THT]
  R2 = Resistor [tolerance=±5% resistance=10k package=THT]
  C1 = Ceramic Capacitor [capacitance=100nF package="100 mil [THT, multilayer]"]
  U1 = LIPO-2000mAh [package=lipo-2000]
  DHT1 = DHT22 Humidity and Temperature Sensor
  R3 = Resistor [tolerance=±5% resistance=10k package=THT]
  S1_-_Reset = Pushbutton [package="[THT]"]
  J2b_-_UART = Dagu DGServo 9g header (male) [package=THT]
  D1 = Rectifier Diode [part_number=1N4001 package="300 mil [THT]"]
  J1-_BOOT = rounded female pin header, 2 pins [form="♀ (female rounded)"]
  Q1_-_BC547 = NPN-Transistor [package="TO92 [THT]"]
  R4 = Resistor [tolerance=±5% resistance=68k package=THT]
  R5 = Resistor [tolerance=±5% resistance=1M package=THT]
  R6 = Photocell (LDR) [package=THT]
  R7 = Resistor [tolerance=±5% resistance=33k package=THT]

nets:
  N1: ESP.REST, ESP.GPIO16, R3.Pin_0, S1_-_Reset.Pin_3, S1_-_Reset.Pin_4
  N2: ESP.ADC, Q1_-_BC547.C, R4.Pin_0, R7.Pin_0
  N3: ESP.CH_PD, R2.Pin_0
  N4: ESP.VCC, R1.Pin_1, R2.Pin_1, R3.Pin_1, D1.cathode, R4.Pin_1
  N5: ESP.TXD, J2b_-_UART.pulse
  N6: ESP.RXD, J2b_-_UART.Vcc
  N7: ESP.GPIO4, R5.Pin_1
  N8: ESP.GPIO5, DHT1.DATA
  N9: ESP.GPIO0, R1.Pin_0, J1-_BOOT.pin1
  GND: ESP.GPIO15, ESP.GND, C1.1, U1.-, DHT1.NULL, DHT1.GND, S1_-_Reset.Pin_1, S1_-_Reset.Pin_2, J2b_-_UART.gnd, J1-_BOOT.pin2, R6.pin_0, R7.Pin_1
  N10: C1.0, U1.+, DHT1.VDD, D1.anode
  N11: Q1_-_BC547.E, R6.pin_1
  N12: Q1_-_BC547.B, R5.Pin_0
