# Fritzing sketch LDR and Voltage Multiplexer (saved by Fritzing 0.9.3b)
breadboards: 1

parts:
  C1 = Ceramic Capacitor [capacitance=100nF package="100 mil [THT, multilayer]"]
  U1 = LIPO-2000mAh [package=lipo-2000]
  D1 = Rectifier Diode [part_number=1N4001 package="300 mil [THT]"]
  Q1_-_BC547 = NPN-Transistor [package="TO92 [THT]"]
  R4 = Resistor [tolerance=±5% resistance=68k package=THT]
  R5 = Resistor [tolerance=±5% resistance=1M package=THT]
  R6 = Photocell (LDR) [package=THT]
  R7 = Resistor [tolerance=±5% resistance=33k package=THT]
  JP1 = Header 2 [package=screwterminal-3.5mm-2_lock]

nets:
  N1: C1.0, U1.+, D1.anode
  N2: C1.1, U1.-, R6.pin_0, R7.Pin_1
  N3: D1.cathode, R4.Pin_1
  N4: Q1_-_BC547.E, R6.pin_1
  N5: Q1_-_BC547.B, R5.Pin_0
  N6: Q1_-_BC547.C, R4.Pin_0, R7.Pin_0, JP1.1
  N7: R5.Pin_1, JP1.2
